# Fritzing sketch dht11 (saved by Fritzing 1.0.8)

parts:
  Part1 = Arduino Uno (Rev3)
  DHT1 = DHT11 Humitidy and Temperature Sensor (3 pins)
  Part2 = LCD1602-I2C

nets:
  N1: Part1.A4/SDA, Part2.SDA
  N2: Part1.A5/SCL, Part2.SCL
  GND: Part1.GND, DHT1.Gnd, Part2.GND
  N3: Part1.D2, DHT1.Signal
  5V: Part1.5V, DHT1.Plus, Part2.VCC

custom parts:
  DHT11 Humitidy and Temperature Sensor (3 pins): DHT11 Humidity and Temperature Sensor (3 pins).
  LCD1602-I2C: A standard character display, usually with 2x16 characters. Comes in many colors with LCM1602 IIC attached.
