# Fritzing sketch dht11_mq (saved by Fritzing 1.0.8)

parts:
  Part1 = Arduino Uno (Rev3)
  Part2 = LCD1602-I2C
  A1 = MQ-2 breakout
  DHT1 = DHT11 Humitidy and Temperature Sensor (3 pins)

nets:
  N1: Part1.A0, A1.DO
  N2: Part1.A4/SDA, Part2.SDA
  N3: Part1.A5/SCL, Part2.SCL
  GND: Part1.GND, Part2.GND, A1.GND, DHT1.Gnd
  N4: Part1.D2, DHT1.Signal
  VCC: Part1.5V, Part2.VCC, A1.VCC, DHT1.Plus

custom parts:
  LCD1602-I2C: A standard character display, usually with 2x16 characters. Comes in many colors with LCM1602 IIC attached.
  MQ-2 breakout: MQ-2 gas sensor
  DHT11 Humitidy and Temperature Sensor (3 pins): DHT11 Humidity and Temperature Sensor (3 pins).
