# Fritzing sketch passive-buzzer (saved by Fritzing 1.0.8)
breadboards: 1

parts:
  Part1 = Arduino Nano (Rev3.0)
  R1 = Resistor [tolerance=±5% power=0.25W resistance=220 package=THT]
  LED1 = LED - 5mm [color="Red (633nm)" current=0.030A package="5 mm [THT]"]

nets:
  N1: Part1.GND, LED1.cathode
  N2: Part1.D9, R1.Pin_1
  N3: R1.Pin_0, LED1.anode
