# Fritzing sketch ultrasonic-3led-lcd-buzzer (saved by Fritzing 1.0.8)
breadboards: 1

parts:
  Part1 = Arduino Nano (Rev3.0)
  HC-SR04_Sensor_1 = HC-SR04 Ultrasonic Distance Sensor
  A1 = BBAA100043
  J1 = Piezo Speaker
  Part2 = LCD1602-I2C

nets:
  GND: Part1.GND, HC-SR04_Sensor_1.GND, A1.pin4, J1.pin1, Part2.GND
  N1: Part1.D4, HC-SR04_Sensor_1.ECHO
  N2: Part1.D5, HC-SR04_Sensor_1.TRIG
  N3: Part1.D6, A1.pin1
  N4: Part1.D7, A1.pin2
  N5: Part1.D8, A1.pin3
  N6: Part1.D9, J1.pin2
  VCC: Part1.5V, HC-SR04_Sensor_1.VCC, Part2.VCC
  N7: Part1.A5, Part2.SCL
  N8: Part1.A4, Part2.SDA

custom parts:
  BBAA100043: BBAA100043 traffic light module.
  LCD1602-I2C: A standard character display, usually with 2x16 characters. Comes in many colors with LCM1602 IIC attached.
