# Fritzing sketch ultrasonic-3led (saved by Fritzing 1.0.8)
breadboards: 1

parts:
  Part1 = Arduino Nano (Rev3.0)
  HC-SR04_Sensor_1 = HC-SR04 Ultrasonic Distance Sensor
  A1 = BBAA100043

nets:
  GND: Part1.GND, HC-SR04_Sensor_1.GND, A1.pin4
  N1: Part1.D4, HC-SR04_Sensor_1.ECHO
  N2: Part1.D5, HC-SR04_Sensor_1.TRIG
  N3: Part1.D6, A1.pin1
  N4: Part1.D7, A1.pin2
  N5: Part1.D8, A1.pin3
  5V: Part1.5V, HC-SR04_Sensor_1.VCC

custom parts:
  BBAA100043: BBAA100043 traffic light module.
