# Fritzing sketch ultrasonic-lcd (saved by Fritzing 1.0.8)
breadboards: 1

parts:
  Part1 = Arduino Nano (Rev3.0)
  Part2 = LCD1602-I2C
  HC-SR04_Sensor_1 = HC-SR04 Ultrasonic Distance Sensor

nets:
  GND: Part1.GND, Part2.GND, HC-SR04_Sensor_1.GND
  N1: Part1.D4, HC-SR04_Sensor_1.ECHO
  N2: Part1.D5, HC-SR04_Sensor_1.TRIG
  VCC: Part1.5V, Part2.VCC, HC-SR04_Sensor_1.VCC
  N3: Part1.A5, Part2.SCL
  N4: Part1.A4, Part2.SDA

custom parts:
  LCD1602-I2C: A standard character display, usually with 2x16 characters. Comes in many colors with LCM1602 IIC attached.
